// Logisim project riscv_simulator.circ as structural Verilog: 1 circuit, main circuit main
module main (
  input  in_1,
  input  [1:0] in_2,
  input  in_3,
  input  in_4,
  input  in_5,
  input  in_6,
  input  in_7,
  input  in_8,
  output [31:0] out_9,
  output [31:0] out_10,
  output [31:0] out_11,
  output [31:0] out_12,
  output [3:0] out_13
);

  wire and_1_out, and_2_out, clock_1_out, clock_2_out, clock_4_out, clock_5_out, clock_6_out, GateMDR,
       GatePC, LD_IR, LD_PC, not_1_out, or_1_out;
  wire [7:0] decoder_2_out0, decoder_2_out8, decoder_2_out16, decoder_2_out24, decoder_3_out0,
       decoder_3_out8, decoder_3_out16, decoder_3_out24;
  wire [15:0] MDR_q, MDR_q_2, ram_1_dout, ram_2_dout;
  wire [30:0] controlled_buffer_18_out;
  wire [31:0] adder_1_out, adder_2_out, and_3_out, bit_extender_1_out, controlled_buffer_1_out, MAR_q,
       multiplexer_1_out, multiplexer_2_out, multiplexer_3_out, multiplexer_4_out, multiplexer_5_out,
       multiplexer_6_out, not_2_out, or_2_out, undriven, undriven_2, x1_q, x2_q, x3_q, x4_q, x5_q, x6_q,
       x7_q, x8_q, x9_q, x10_q, x11_q, x12_q, x13_q, x14_q, x15_q, x16_q, x17_q, x18_q, x19_q, x20_q, x21_q,
       x22_q, x23_q, x24_q, x25_q, x26_q, x27_q, x28_q, x29_q, x30_q, x31_q, xor_1_out, xor_2_out;
  wire [31:1] decoder_1_out1;

  Register #(.width(32)) IR (
    .D({out_13[2], controlled_buffer_18_out}), .en(LD_IR), .clk(clock_1_out), .Q(out_9));  // open: clr
  Clock clock_1 (.out(clock_1_out));
  Clock clock_2 (.out(clock_2_out));
  Register #(.width(32)) MAR (
    .D({out_13[2], controlled_buffer_18_out}), .en(in_4), .clk(clock_2_out), .Q(MAR_q), .clr(in_1));
  and and_1 (and_1_out, in_7, in_8);
  Clock clock_3 ();  // open: out
  RAM #(.addrWidth(16), .dataWidth(16)) ram_1 (
    .addr(MAR_q[31:16]), .we(and_1_out), .oe(and_2_out), .clk(clock_2_out), .din(MDR_q_2), .dout(ram_1_dout));
  and and_2 (and_2_out, in_8, ~in_7);  // AND_Gate
  not not_1 (not_1_out, in_1);
  Multiplexer #(.width(32)) multiplexer_1 (
    .in0(32'hdeadbeef), .in1(multiplexer_2_out), .out(multiplexer_1_out), .sel(not_1_out));
  or or_1 (or_1_out, in_1, LD_PC);
  Clock clock_4 (.out(clock_4_out));
  Multiplexer #(.select(2), .width(32)) multiplexer_2 (
    .in0(adder_1_out), .in1(undriven), .in2(undriven_2), .out(multiplexer_2_out), .sel(in_2));  // open: in3
  Register #(.width(32)) PC (.D(multiplexer_1_out), .en(or_1_out), .clk(clock_4_out), .Q(out_10));  // open: clr
  Adder #(.width(32)) adder_1 (.a(32'h4), .b(out_10), .out(adder_1_out));  // open: cin, cout
  assign controlled_buffer_1_out = GatePC ? out_10 : 32'bz;  // Controlled_Buffer controlled_buffer_1
  RAM #(.addrWidth(16), .dataWidth(16)) ram_2 (
    .addr(MAR_q[15:0]), .we(and_1_out), .oe(and_2_out), .clk(clock_2_out), .din(MDR_q), .dout(ram_2_dout));
  Decoder #(.select(5)) decoder_1 (
    .out1(decoder_1_out1[1]), .out2(decoder_1_out1[2]), .out3(decoder_1_out1[3]), .out4(decoder_1_out1[4]),
    .out5(decoder_1_out1[5]), .out6(decoder_1_out1[6]), .out7(decoder_1_out1[7]), .out8(decoder_1_out1[8]),
    .out9(decoder_1_out1[9]), .out10(decoder_1_out1[10]), .out11(decoder_1_out1[11]),
    .out12(decoder_1_out1[12]), .out13(decoder_1_out1[13]), .out14(decoder_1_out1[14]),
    .out15(decoder_1_out1[15]), .out16(decoder_1_out1[16]), .out17(decoder_1_out1[17]),
    .out18(decoder_1_out1[18]), .out19(decoder_1_out1[19]), .out20(decoder_1_out1[20]),
    .out21(decoder_1_out1[21]), .out22(decoder_1_out1[22]), .out23(decoder_1_out1[23]),
    .out24(decoder_1_out1[24]), .out25(decoder_1_out1[25]), .out26(decoder_1_out1[26]),
    .out27(decoder_1_out1[27]), .out28(decoder_1_out1[28]), .out29(decoder_1_out1[29]),
    .out30(decoder_1_out1[30]), .out31(decoder_1_out1[31]), .sel(out_9[11:7]), .en(in_3));  // open: out0
  Clock clock_5 (.out(clock_5_out));
  Register #(.width(32)) x1 (.D(32'hdeadbeef), .en(decoder_1_out1[1]), .clk(clock_5_out), .Q(x1_q));  // open: clr
  Register #(.width(32)) x2 (.D(32'hdeadbeef), .en(decoder_1_out1[2]), .clk(clock_5_out), .Q(x2_q));  // open: clr
  Register #(.width(32)) x3 (.D(32'hdeadbeef), .en(decoder_1_out1[3]), .clk(clock_5_out), .Q(x3_q));  // open: clr
  Register #(.width(32)) x4 (.D(32'hdeadbeef), .en(decoder_1_out1[4]), .clk(clock_5_out), .Q(x4_q));  // open: clr
  Register #(.width(32)) x5 (.D(32'hdeadbeef), .en(decoder_1_out1[5]), .clk(clock_5_out), .Q(x5_q));  // open: clr
  Register #(.width(32)) x6 (.D(32'hdeadbeef), .en(decoder_1_out1[6]), .clk(clock_5_out), .Q(x6_q));  // open: clr
  Register #(.width(32)) x7 (.D(32'hdeadbeef), .en(decoder_1_out1[7]), .clk(clock_5_out), .Q(x7_q));  // open: clr
  Multiplexer #(.width(32)) multiplexer_3 (
    .in0({out_13[2], controlled_buffer_18_out}), .in1(multiplexer_4_out), .out(multiplexer_3_out), .sel(in_6));
  Multiplexer #(.select(2), .width(32)) multiplexer_4 (
    .in0({32{1'b0}}), .in1({32{1'b0}}), .in2({32{1'b0}}), .in3({ram_1_dout, ram_2_dout}),
    .out(multiplexer_4_out));  // open: sel
  // Probe on {ram_1_dout, ram_2_dout}
  Register #(.width(32)) MDR (.D(multiplexer_3_out), .en(in_5), .clk(clock_6_out), .Q({MDR_q_2, MDR_q}), .clr(in_1));
  Clock clock_6 (.out(clock_6_out));
  assign out_11 = decoder_2_out0[0] ? {32{1'b0}} : 32'bz;  // Controlled_Buffer controlled_buffer_2
  assign out_12 = decoder_3_out0[0] ? {32{1'b0}} : 32'bz;  // Controlled_Buffer controlled_buffer_3
  assign out_11 = decoder_2_out0[1] ? x1_q : 32'bz;  // Controlled_Buffer controlled_buffer_4
  assign out_12 = decoder_3_out0[1] ? x1_q : 32'bz;  // Controlled_Buffer controlled_buffer_5
  assign out_11 = decoder_2_out0[2] ? x2_q : 32'bz;  // Controlled_Buffer controlled_buffer_6
  assign out_12 = decoder_3_out0[2] ? x2_q : 32'bz;  // Controlled_Buffer controlled_buffer_7
  assign out_11 = decoder_2_out0[3] ? x3_q : 32'bz;  // Controlled_Buffer controlled_buffer_8
  assign out_12 = decoder_3_out0[3] ? x3_q : 32'bz;  // Controlled_Buffer controlled_buffer_9
  assign out_11 = decoder_2_out0[4] ? x4_q : 32'bz;  // Controlled_Buffer controlled_buffer_10
  assign out_12 = decoder_3_out0[4] ? x4_q : 32'bz;  // Controlled_Buffer controlled_buffer_11
  assign out_11 = decoder_2_out0[5] ? x5_q : 32'bz;  // Controlled_Buffer controlled_buffer_12
  assign out_12 = decoder_3_out0[5] ? x5_q : 32'bz;  // Controlled_Buffer controlled_buffer_13
  assign out_11 = decoder_2_out0[6] ? x6_q : 32'bz;  // Controlled_Buffer controlled_buffer_14
  assign out_12 = decoder_3_out0[6] ? x6_q : 32'bz;  // Controlled_Buffer controlled_buffer_15
  assign out_11 = decoder_2_out0[7] ? x7_q : 32'bz;  // Controlled_Buffer controlled_buffer_16
  assign out_12 = decoder_3_out0[7] ? x7_q : 32'bz;  // Controlled_Buffer controlled_buffer_17
  Register #(.width(32)) x8 (.D(32'hdeadbeef), .en(decoder_1_out1[8]), .clk(clock_5_out), .Q(x8_q));  // open: clr
  Register #(.width(32)) x9 (.D(32'hdeadbeef), .en(decoder_1_out1[9]), .clk(clock_5_out), .Q(x9_q));  // open: clr
  Register #(.width(32)) x10 (.D(32'hdeadbeef), .en(decoder_1_out1[10]), .clk(clock_5_out), .Q(x10_q));  // open: clr
  Register #(.width(32)) x11 (.D(32'hdeadbeef), .en(decoder_1_out1[11]), .clk(clock_5_out), .Q(x11_q));  // open: clr
  Register #(.width(32)) x12 (.D(32'hdeadbeef), .en(decoder_1_out1[12]), .clk(clock_5_out), .Q(x12_q));  // open: clr
  Register #(.width(32)) x13 (.D(32'hdeadbeef), .en(decoder_1_out1[13]), .clk(clock_5_out), .Q(x13_q));  // open: clr
  Register #(.width(32)) x14 (.D(32'hdeadbeef), .en(decoder_1_out1[14]), .clk(clock_5_out), .Q(x14_q));  // open: clr
  Register #(.width(32)) x15 (.D(32'hdeadbeef), .en(decoder_1_out1[15]), .clk(clock_5_out), .Q(x15_q));  // open: clr
  assign {out_13[2], controlled_buffer_18_out} = GateMDR ? {MDR_q_2, MDR_q} : 32'bz;  // Controlled_Buffer controlled_buffer_18
  assign out_11 = decoder_2_out8[0] ? x8_q : 32'bz;  // Controlled_Buffer controlled_buffer_19
  assign out_11 = decoder_2_out8[1] ? x9_q : 32'bz;  // Controlled_Buffer controlled_buffer_20
  assign out_11 = decoder_2_out8[2] ? x10_q : 32'bz;  // Controlled_Buffer controlled_buffer_21
  assign out_11 = decoder_2_out8[3] ? x11_q : 32'bz;  // Controlled_Buffer controlled_buffer_22
  assign out_11 = decoder_2_out8[4] ? x12_q : 32'bz;  // Controlled_Buffer controlled_buffer_23
  assign out_11 = decoder_2_out8[5] ? x13_q : 32'bz;  // Controlled_Buffer controlled_buffer_24
  assign out_11 = decoder_2_out8[6] ? x14_q : 32'bz;  // Controlled_Buffer controlled_buffer_25
  assign out_11 = decoder_2_out8[7] ? x15_q : 32'bz;  // Controlled_Buffer controlled_buffer_26
  Register #(.width(32)) x16 (.D(32'hdeadbeef), .en(decoder_1_out1[16]), .clk(clock_5_out), .Q(x16_q));  // open: clr
  assign out_12 = decoder_3_out8[0] ? x8_q : 32'bz;  // Controlled_Buffer controlled_buffer_27
  Register #(.width(32)) x17 (.D(32'hdeadbeef), .en(decoder_1_out1[17]), .clk(clock_5_out), .Q(x17_q));  // open: clr
  assign out_12 = decoder_3_out8[1] ? x9_q : 32'bz;  // Controlled_Buffer controlled_buffer_28
  Register #(.width(32)) x18 (.D(32'hdeadbeef), .en(decoder_1_out1[18]), .clk(clock_5_out), .Q(x18_q));  // open: clr
  assign out_12 = decoder_3_out8[2] ? x10_q : 32'bz;  // Controlled_Buffer controlled_buffer_29
  Register #(.width(32)) x19 (.D(32'hdeadbeef), .en(decoder_1_out1[19]), .clk(clock_5_out), .Q(x19_q));  // open: clr
  assign out_12 = decoder_3_out8[3] ? x11_q : 32'bz;  // Controlled_Buffer controlled_buffer_30
  Register #(.width(32)) x20 (.D(32'hdeadbeef), .en(decoder_1_out1[20]), .clk(clock_5_out), .Q(x20_q));  // open: clr
  assign out_12 = decoder_3_out8[4] ? x12_q : 32'bz;  // Controlled_Buffer controlled_buffer_31
  Register #(.width(32)) x21 (.D(32'hdeadbeef), .en(decoder_1_out1[21]), .clk(clock_5_out), .Q(x21_q));  // open: clr
  assign out_12 = decoder_3_out8[5] ? x13_q : 32'bz;  // Controlled_Buffer controlled_buffer_32
  Register #(.width(32)) x22 (.D(32'hdeadbeef), .en(decoder_1_out1[22]), .clk(clock_5_out), .Q(x22_q));  // open: clr
  assign out_12 = decoder_3_out8[6] ? x14_q : 32'bz;  // Controlled_Buffer controlled_buffer_33
  Register #(.width(32)) x23 (.D(32'hdeadbeef), .en(decoder_1_out1[23]), .clk(clock_5_out), .Q(x23_q));  // open: clr
  assign out_12 = decoder_3_out8[7] ? x15_q : 32'bz;  // Controlled_Buffer controlled_buffer_34
  Multiplexer #(.width(32)) multiplexer_5 (.in0(32'h2), .in1({32{1'b0}}), .out(multiplexer_5_out), .sel(1'b1));
  assign xor_1_out = 32'h1 ^ bit_extender_1_out;  // XOR_Gate xor_1, 32 bits wide
  assign bit_extender_1_out = {{31{1'b0}}, 1'b0};  // Bit_Extender bit_extender_1
  assign out_11 = decoder_2_out16[0] ? x16_q : 32'bz;  // Controlled_Buffer controlled_buffer_35
  assign out_12 = decoder_3_out16[0] ? x16_q : 32'bz;  // Controlled_Buffer controlled_buffer_36
  assign out_11 = decoder_2_out16[1] ? x17_q : 32'bz;  // Controlled_Buffer controlled_buffer_37
  assign out_12 = decoder_3_out16[1] ? x17_q : 32'bz;  // Controlled_Buffer controlled_buffer_38
  assign out_11 = decoder_2_out16[2] ? x18_q : 32'bz;  // Controlled_Buffer controlled_buffer_39
  assign out_12 = decoder_3_out16[2] ? x18_q : 32'bz;  // Controlled_Buffer controlled_buffer_40
  assign out_11 = decoder_2_out16[3] ? x19_q : 32'bz;  // Controlled_Buffer controlled_buffer_41
  assign out_12 = decoder_3_out16[3] ? x19_q : 32'bz;  // Controlled_Buffer controlled_buffer_42
  assign out_11 = decoder_2_out16[4] ? x20_q : 32'bz;  // Controlled_Buffer controlled_buffer_43
  assign out_12 = decoder_3_out16[4] ? x20_q : 32'bz;  // Controlled_Buffer controlled_buffer_44
  assign out_11 = decoder_2_out16[5] ? x21_q : 32'bz;  // Controlled_Buffer controlled_buffer_45
  assign out_12 = decoder_3_out16[5] ? x21_q : 32'bz;  // Controlled_Buffer controlled_buffer_46
  assign out_11 = decoder_2_out16[6] ? x22_q : 32'bz;  // Controlled_Buffer controlled_buffer_47
  assign out_12 = decoder_3_out16[6] ? x22_q : 32'bz;  // Controlled_Buffer controlled_buffer_48
  assign out_11 = decoder_2_out16[7] ? x23_q : 32'bz;  // Controlled_Buffer controlled_buffer_49
  assign out_12 = decoder_3_out16[7] ? x23_q : 32'bz;  // Controlled_Buffer controlled_buffer_50
  assign and_3_out = 32'h2 & 32'h1;  // AND_Gate and_3, 32 bits wide
  assign or_2_out = 32'h2 | 32'h1;  // OR_Gate or_2, 32 bits wide
  Multiplexer #(.select(2), .width(32)) multiplexer_6 (
    .in0(and_3_out), .in1(or_2_out), .in2(xor_2_out), .in3(not_2_out), .out(multiplexer_6_out), .sel(2'b11));
  assign xor_2_out = 32'h2 ^ 32'h1;  // XOR_Gate xor_2, 32 bits wide
  assign not_2_out = ~32'h1;  // NOT_Gate not_2, 32 bits wide
  Register #(.width(32)) x24 (.D(32'hdeadbeef), .en(decoder_1_out1[24]), .clk(clock_5_out), .Q(x24_q));  // open: clr
  Register #(.width(32)) x25 (.D(32'hdeadbeef), .en(decoder_1_out1[25]), .clk(clock_5_out), .Q(x25_q));  // open: clr
  Register #(.width(32)) x26 (.D(32'hdeadbeef), .en(decoder_1_out1[26]), .clk(clock_5_out), .Q(x26_q));  // open: clr
  Register #(.width(32)) x27 (.D(32'hdeadbeef), .en(decoder_1_out1[27]), .clk(clock_5_out), .Q(x27_q));  // open: clr
  Register #(.width(32)) x28 (.D(32'hdeadbeef), .en(decoder_1_out1[28]), .clk(clock_5_out), .Q(x28_q));  // open: clr
  Register #(.width(32)) x29 (.D(32'hdeadbeef), .en(decoder_1_out1[29]), .clk(clock_5_out), .Q(x29_q));  // open: clr
  Register #(.width(32)) x30 (.D(32'hdeadbeef), .en(decoder_1_out1[30]), .clk(clock_5_out), .Q(x30_q));  // open: clr
  Register #(.width(32)) x31 (.D(32'hdeadbeef), .en(decoder_1_out1[31]), .clk(clock_5_out), .Q(x31_q));  // open: clr
  Multiplexer #(.width(32)) multiplexer_7 (
    .in0(multiplexer_6_out), .in1(adder_2_out), .out({out_13[2], controlled_buffer_18_out}), .sel(1'b0));
  Adder #(.width(32)) adder_2 (.a(multiplexer_5_out), .b(xor_1_out), .out(adder_2_out), .cin(1'b1), .cout(out_13[3]));
  assign out_11 = decoder_2_out24[0] ? x24_q : 32'bz;  // Controlled_Buffer controlled_buffer_51
  assign out_12 = decoder_3_out24[0] ? x24_q : 32'bz;  // Controlled_Buffer controlled_buffer_52
  assign out_11 = decoder_2_out24[1] ? x25_q : 32'bz;  // Controlled_Buffer controlled_buffer_53
  assign out_12 = decoder_3_out24[1] ? x25_q : 32'bz;  // Controlled_Buffer controlled_buffer_54
  assign out_11 = decoder_2_out24[2] ? x26_q : 32'bz;  // Controlled_Buffer controlled_buffer_55
  assign out_12 = decoder_3_out24[2] ? x26_q : 32'bz;  // Controlled_Buffer controlled_buffer_56
  assign out_11 = decoder_2_out24[3] ? x27_q : 32'bz;  // Controlled_Buffer controlled_buffer_57
  assign out_12 = decoder_3_out24[3] ? x27_q : 32'bz;  // Controlled_Buffer controlled_buffer_58
  assign out_11 = decoder_2_out24[4] ? x28_q : 32'bz;  // Controlled_Buffer controlled_buffer_59
  assign out_12 = decoder_3_out24[4] ? x28_q : 32'bz;  // Controlled_Buffer controlled_buffer_60
  assign out_11 = decoder_2_out24[5] ? x29_q : 32'bz;  // Controlled_Buffer controlled_buffer_61
  assign out_12 = decoder_3_out24[5] ? x29_q : 32'bz;  // Controlled_Buffer controlled_buffer_62
  assign out_11 = decoder_2_out24[6] ? x30_q : 32'bz;  // Controlled_Buffer controlled_buffer_63
  assign out_12 = decoder_3_out24[6] ? x30_q : 32'bz;  // Controlled_Buffer controlled_buffer_64
  assign out_11 = decoder_2_out24[7] ? x31_q : 32'bz;  // Controlled_Buffer controlled_buffer_65
  assign out_12 = decoder_3_out24[7] ? x31_q : 32'bz;  // Controlled_Buffer controlled_buffer_66
  // Probe on {out_13[2], controlled_buffer_18_out}
  Decoder #(.select(5)) decoder_2 (
    .out0(decoder_2_out0[0]), .out1(decoder_2_out0[1]), .out2(decoder_2_out0[2]), .out3(decoder_2_out0[3]),
    .out4(decoder_2_out0[4]), .out5(decoder_2_out0[5]), .out6(decoder_2_out0[6]), .out7(decoder_2_out0[7]),
    .out8(decoder_2_out8[0]), .out9(decoder_2_out8[1]), .out10(decoder_2_out8[2]), .out11(decoder_2_out8[3]),
    .out12(decoder_2_out8[4]), .out13(decoder_2_out8[5]), .out14(decoder_2_out8[6]),
    .out15(decoder_2_out8[7]), .out16(decoder_2_out16[0]), .out17(decoder_2_out16[1]),
    .out18(decoder_2_out16[2]), .out19(decoder_2_out16[3]), .out20(decoder_2_out16[4]),
    .out21(decoder_2_out16[5]), .out22(decoder_2_out16[6]), .out23(decoder_2_out16[7]),
    .out24(decoder_2_out24[0]), .out25(decoder_2_out24[1]), .out26(decoder_2_out24[2]),
    .out27(decoder_2_out24[3]), .out28(decoder_2_out24[4]), .out29(decoder_2_out24[5]),
    .out30(decoder_2_out24[6]), .out31(decoder_2_out24[7]), .sel(out_9[19:15]));  // open: en
  Decoder #(.select(5)) decoder_3 (
    .out0(decoder_3_out0[0]), .out1(decoder_3_out0[1]), .out2(decoder_3_out0[2]), .out3(decoder_3_out0[3]),
    .out4(decoder_3_out0[4]), .out5(decoder_3_out0[5]), .out6(decoder_3_out0[6]), .out7(decoder_3_out0[7]),
    .out8(decoder_3_out8[0]), .out9(decoder_3_out8[1]), .out10(decoder_3_out8[2]), .out11(decoder_3_out8[3]),
    .out12(decoder_3_out8[4]), .out13(decoder_3_out8[5]), .out14(decoder_3_out8[6]),
    .out15(decoder_3_out8[7]), .out16(decoder_3_out16[0]), .out17(decoder_3_out16[1]),
    .out18(decoder_3_out16[2]), .out19(decoder_3_out16[3]), .out20(decoder_3_out16[4]),
    .out21(decoder_3_out16[5]), .out22(decoder_3_out16[6]), .out23(decoder_3_out16[7]),
    .out24(decoder_3_out24[0]), .out25(decoder_3_out24[1]), .out26(decoder_3_out24[2]),
    .out27(decoder_3_out24[3]), .out28(decoder_3_out24[4]), .out29(decoder_3_out24[5]),
    .out30(decoder_3_out24[6]), .out31(decoder_3_out24[7]), .sel(out_9[24:20]));  // open: en
  xor xor_3 (out_13[0], out_13[3], adder_2_out[31]);
  nor nor_1 (out_13[1], out_13[2], controlled_buffer_18_out[30], controlled_buffer_18_out[29], controlled_buffer_18_out[28], controlled_buffer_18_out[27], controlled_buffer_18_out[26], controlled_buffer_18_out[25], controlled_buffer_18_out[24], controlled_buffer_18_out[23], controlled_buffer_18_out[22], controlled_buffer_18_out[21], controlled_buffer_18_out[20], controlled_buffer_18_out[19], controlled_buffer_18_out[18], controlled_buffer_18_out[17], controlled_buffer_18_out[16], controlled_buffer_18_out[15], controlled_buffer_18_out[14], controlled_buffer_18_out[13], controlled_buffer_18_out[12], controlled_buffer_18_out[11], controlled_buffer_18_out[10], controlled_buffer_18_out[9], controlled_buffer_18_out[8], controlled_buffer_18_out[7], controlled_buffer_18_out[6], controlled_buffer_18_out[5], controlled_buffer_18_out[4], controlled_buffer_18_out[3], controlled_buffer_18_out[2], controlled_buffer_18_out[1], controlled_buffer_18_out[0]);

  // Other names for the same wires on the sheet: C_MDR = in_6; CNZV[3:0] = out_13;
  //   immB[12:1] = {out_9[31], out_9[7], out_9[30:25], out_9[11:8]}; immS[11:0] = {out_9[31:25], out_9[11:7]};
  //   Instr[31:0] = out_9; rd[4:0] = out_9[11:7]; funct3[2:0] = out_9[14:12];
  //   immJ[20:1] = {out_9[31], out_9[19:12], out_9[20], out_9[30:21]}; immU[31:12] = out_9[31:12];
  //   rs1[4:0] = out_9[19:15]; immI[11:0] = out_9[31:20]; rs2[4:0] = out_9[24:20]; funct7[6:0] = out_9[31:25];
  //   SE = out_9[31]; opcode[6:0] = out_9[6:0]; LD_MAR = in_4; LD_MDR = in_5; LD_REG = in_3; MEM_EN = in_8;
  //   PC[31:0] = out_10; PCMUX[1:0] = in_2; R_W = in_7; ResetSim = in_1; SR1[31:0] = out_11; SR2[31:0] = out_12

  // Notes on the sheet:
  //   Memory
  //   DR
  //   REGISTER FILE
  //   I/O Mem Mapping
  //   ALU
  //   ALU_OUT
  //   SR1
  //   SR2
endmodule
